// Logisim project KEDVAC_RAMSEY.circ as structural Verilog: 7 circuits, main circuit main
module main (
  input  [7:0] Address,
  input  Read_0__Write_1,
  input  [7:0] Data_in_if_any,
  input  Clock,
  output [7:0] Data
);

  wire and_1_out, not_1_out, not_2_out;
  wire [4:0] controlled_buffer_1_out, controlled_buffer_2_out;
  wire [7:0] controlled_buffer_6_out, ram_1_data, rom_1_data;

  assign controlled_buffer_1_out = not_1_out ? Address[4:0] : 5'bz;  // Controlled_Buffer controlled_buffer_1
  assign controlled_buffer_2_out = and_1_out ? Address[4:0] : 5'bz;  // Controlled_Buffer controlled_buffer_2
  not not_1 (not_1_out, and_1_out);
  and and_1 (and_1_out, Address[3], Address[4]);
  ROM #(.addrWidth(5)) rom_1 (.addr(controlled_buffer_1_out), .data(rom_1_data));  // open: sel
  RAM #(.addrWidth(5)) ram_1 (
    .addr(controlled_buffer_2_out), .data(ram_1_data), .clk(Clock), .ld(not_2_out));  // open: sel, clr
  assign Data = not_1_out ? rom_1_data : 8'bz;  // Controlled_Buffer controlled_buffer_3
  assign ram_1_data = Read_0__Write_1 ? Data_in_if_any : 8'bz;  // Controlled_Buffer controlled_buffer_4
  assign Data = and_1_out ? controlled_buffer_6_out : 8'bz;  // Controlled_Buffer controlled_buffer_5
  assign controlled_buffer_6_out = not_2_out ? ram_1_data : 8'bz;  // Controlled_Buffer controlled_buffer_6
  not not_2 (not_2_out, Read_0__Write_1);

  // Notes on the sheet:
  //   contents of rom_1 (hex, n*v repeats v):
  //   f ce b0 11*0 9 10
endmodule

module bigComputer (
);

  wire A_MB, Clock, clock_1_out, flag, IC_1_IC, IC_MA, ldA, ldB, ldIC, ldMA, ldMB, ldOP, ldxmp, MB_IC, MB_MA,
       R, Read_0__Write_1, Sub, zero;
  wire [2:0] OP_q_2;
  wire [4:0] OP_q;
  wire [6:0] xmp_q;
  wire [7:0] A_q, alu_1_out_4, and_1_out, B_q, controlled_buffer_1_out, controlled_buffer_2_out,
       controlled_buffer_3_out, controlled_buffer_5_out, IC_q, MA_q, main_1_data, MB_q, n8_bit_adder_1_out_3;
  wire [7:7] not_1_out;

  main main_1 (
    .Address(MA_q), .Data_in_if_any(controlled_buffer_3_out), .Data(main_1_data), .Clock(Clock),
    .Read_0__Write_1(Read_0__Write_1));
  Register MA (.D(controlled_buffer_1_out), .en(ldMA), .Q(MA_q), .clk(Clock));  // open: clr
  assign controlled_buffer_1_out = IC_MA ? IC_q : 8'bz;  // Controlled_Buffer controlled_buffer_1
  assign controlled_buffer_2_out = R ? main_1_data : 8'bz;  // Controlled_Buffer controlled_buffer_2
  assign controlled_buffer_3_out = Read_0__Write_1 ? MB_q : 8'bz;  // Controlled_Buffer controlled_buffer_3
  assign controlled_buffer_1_out = MB_MA ? MB_q : 8'bz;  // Controlled_Buffer controlled_buffer_4
  Register MB (.D(controlled_buffer_2_out), .en(ldMB), .Q(MB_q), .clk(Clock));  // open: clr
  assign controlled_buffer_5_out = MB_IC ? MB_q : 8'bz;  // Controlled_Buffer controlled_buffer_5
  assign controlled_buffer_2_out = A_MB ? A_q : 8'bz;  // Controlled_Buffer controlled_buffer_6
  ALU alu_1 (.Sub(Sub), .out_4(alu_1_out_4), .in_2(B_q), .A(and_1_out));
  assign controlled_buffer_5_out = IC_1_IC ? n8_bit_adder_1_out_3 : 8'bz;  // Controlled_Buffer controlled_buffer_7
  Register IC (.D(controlled_buffer_5_out), .en(ldIC), .Q(IC_q), .clk(Clock));  // open: clr
  Register B (.D(MB_q), .en(ldB), .Q(B_q), .clk(Clock));  // open: clr
  Register A (.D(alu_1_out_4), .en(ldA), .Q(A_q), .clk(Clock));  // open: clr
  _8_bit_adder u_8_bit_adder_1 (.out_3(n8_bit_adder_1_out_3), .in_1(IC_q), .in_2(8'h1));
  assign and_1_out = A_q & {8{not_1_out[7]}};  // AND_Gate and_1, 8 bits wide
  not not_1 (not_1_out[7], zero);
  Register xmp (.D(alu_1_out_4), .en(ldxmp), .Q({flag, xmp_q}), .clk(Clock));  // open: clr
  Clock clock_1 (.out(clock_1_out));
  Register OP (.D(MB_q), .en(ldOP), .Q({OP_q_2, OP_q}), .clk(Clock));  // open: clr
  decoder decoder_1 (
    .Clock(clock_1_out), .Opcode(OP_q_2), .A_MB(A_MB), .Clock_2(Clock), .IC_MA(IC_MA), .IC_1_IC(IC_1_IC),
    .MB_IC(MB_IC), .ldMB(ldMB), .MB_MA(MB_MA), .ldB(ldB), .Sub(Sub), .ldA(ldA), .R(R), .ldIC(ldIC),
    .Zero(zero), .ldMA(ldMA), .ldOP(ldOP), .ldxmp(ldxmp), .flag(flag));
  not not_2 (Read_0__Write_1, R);

  // Other names for the same wires on the sheet: W = Read_0__Write_1
endmodule

module Counter (
  input  Clock,
  output t1,
  output t2,
  output t3,
  output t4,
  output t8,
  output t7,
  output t6,
  output t5
);

  wire d_ff_4_qn;
  wire [3:0] d_ff_1_q;

  D_Flip_Flop d_ff_1 (.clk(Clock), .D(d_ff_4_qn), .Q(d_ff_1_q[0]));  // open: Qn, preset, en, reset
  D_Flip_Flop d_ff_2 (.clk(Clock), .D(d_ff_1_q[0]), .Q(d_ff_1_q[1]));  // open: Qn, preset, en, reset
  D_Flip_Flop d_ff_3 (.clk(Clock), .D(d_ff_1_q[1]), .Q(d_ff_1_q[2]));  // open: Qn, preset, en, reset
  D_Flip_Flop d_ff_4 (.clk(Clock), .D(d_ff_1_q[2]), .Q(d_ff_1_q[3]), .Qn(d_ff_4_qn));  // open: preset, en, reset
  Demultiplexer #(.select(4)) demultiplexer_1 (
    .out0(t1), .out1(t2), .out3(t3), .out7(t4), .out8(t8), .out12(t7), .out14(t6), .out15(t5), .in(1'b1),
    .sel(d_ff_1_q));  // open: out2, out4, out5, out6, out9, out10, out11, out13, en
endmodule

module adder (
  input  A,
  input  B,
  input  C,
  output Sum,
  output Carry_Out
);

  wire and_1_out, and_2_out, xor_1_out;

  xor xor_1 (xor_1_out, A, B);
  and and_1 (and_1_out, xor_1_out, C);
  and and_2 (and_2_out, A, B);
  xor xor_2 (Sum, C, xor_1_out);
  or or_1 (Carry_Out, and_1_out, and_2_out);
endmodule

module ALU (
  input  Sub,
  input  [7:0] in_2,
  input  [7:0] A,
  output [7:0] out_4
);

  wire adder_1_carry_out, adder_2_carry_out, adder_3_carry_out, adder_4_carry_out, adder_5_carry_out,
       adder_6_carry_out, adder_8_carry_out;
  wire [7:0] and_1_out, n8_bit_adder_1_out_3, xor_1_out;

  _8_bit_adder u_8_bit_adder_1 (.out_3(n8_bit_adder_1_out_3), .in_1(and_1_out), .in_2(xor_1_out));
  assign xor_1_out = {8{Sub}} ^ in_2;  // XOR_Gate xor_1, 8 bits wide
  assign and_1_out = {8{Sub}} & 8'h1;  // AND_Gate and_1, 8 bits wide
  adder adder_1 (.A(n8_bit_adder_1_out_3[0]), .B(A[0]), .C(1'b0), .Sum(out_4[0]), .Carry_Out(adder_1_carry_out));
  adder adder_2 (
    .A(n8_bit_adder_1_out_3[5]), .B(A[5]), .C(adder_8_carry_out), .Sum(out_4[5]),
    .Carry_Out(adder_2_carry_out));
  adder adder_3 (
    .A(n8_bit_adder_1_out_3[1]), .B(A[1]), .C(adder_1_carry_out), .Sum(out_4[1]),
    .Carry_Out(adder_3_carry_out));
  adder adder_4 (
    .A(n8_bit_adder_1_out_3[6]), .B(A[6]), .C(adder_2_carry_out), .Sum(out_4[6]),
    .Carry_Out(adder_4_carry_out));
  adder adder_5 (
    .A(n8_bit_adder_1_out_3[2]), .B(A[2]), .C(adder_3_carry_out), .Sum(out_4[2]),
    .Carry_Out(adder_5_carry_out));
  adder adder_6 (
    .A(n8_bit_adder_1_out_3[3]), .B(A[3]), .C(adder_5_carry_out), .Sum(out_4[3]),
    .Carry_Out(adder_6_carry_out));
  adder adder_7 (.A(n8_bit_adder_1_out_3[7]), .B(A[7]), .C(adder_4_carry_out), .Sum(out_4[7]));  // open: Carry_Out
  adder adder_8 (
    .A(n8_bit_adder_1_out_3[4]), .B(A[4]), .C(adder_6_carry_out), .Sum(out_4[4]),
    .Carry_Out(adder_8_carry_out));
endmodule

module _8_bit_adder (
  input  [7:0] in_1,
  input  [7:0] in_2,
  output [7:0] out_3
);

  wire adder_1_carry_out, adder_2_carry_out, adder_3_carry_out, adder_4_carry_out, adder_5_carry_out,
       adder_6_carry_out, adder_8_carry_out;

  adder adder_1 (.A(in_1[0]), .B(in_2[0]), .C(1'b0), .Sum(out_3[0]), .Carry_Out(adder_1_carry_out));
  adder adder_2 (.A(in_1[5]), .B(in_2[5]), .C(adder_8_carry_out), .Sum(out_3[5]), .Carry_Out(adder_2_carry_out));
  adder adder_3 (.A(in_1[1]), .B(in_2[1]), .C(adder_1_carry_out), .Sum(out_3[1]), .Carry_Out(adder_3_carry_out));
  adder adder_4 (.A(in_1[6]), .B(in_2[6]), .C(adder_2_carry_out), .Sum(out_3[6]), .Carry_Out(adder_4_carry_out));
  adder adder_5 (.A(in_1[2]), .B(in_2[2]), .C(adder_3_carry_out), .Sum(out_3[2]), .Carry_Out(adder_5_carry_out));
  adder adder_6 (.A(in_1[3]), .B(in_2[3]), .C(adder_5_carry_out), .Sum(out_3[3]), .Carry_Out(adder_6_carry_out));
  adder adder_7 (.A(in_1[7]), .B(in_2[7]), .C(adder_4_carry_out), .Sum(out_3[7]));  // open: Carry_Out
  adder adder_8 (.A(in_1[4]), .B(in_2[4]), .C(adder_6_carry_out), .Sum(out_3[4]), .Carry_Out(adder_8_carry_out));
endmodule

module decoder (
  input  Clock,
  input  [2:0] Opcode,
  input  flag,
  output ldMB,
  output ldOP,
  output Clock_2,
  output MB_MA,
  output ldB,
  output ldMA,
  output ldA,
  output IC_MA,
  output ldIC,
  output Zero,
  output Sub,
  output IC_1_IC,
  output A_MB,
  output R,
  output MB_IC,
  output ldxmp
);

  wire and_2_out, and_3_out, and_4_out, and_5_out, and_6_out, and_7_out, and_8_out, and_9_out, and_11_out,
       and_13_out, and_15_out, counter_1_t1, counter_1_t3, counter_1_t4, counter_1_t5, counter_1_t6,
       counter_1_t7, not_1_out, not_2_out, not_3_out, not_4_out, or_2_out, or_3_out, or_4_out, or_10_out,
       xor_1_out;

  Counter counter_1 (
    .t1(counter_1_t1), .t2(ldOP), .t3(counter_1_t3), .t4(counter_1_t4), .t5(counter_1_t5), .t6(counter_1_t6),
    .t7(counter_1_t7), .t8(IC_MA), .Clock(Clock));
  and and_1 (Zero, ~Opcode[0], ~Opcode[1], ~Opcode[2]);  // AND_Gate
  and and_2 (and_2_out, Opcode[0], ~Opcode[1], ~Opcode[2]);  // AND_Gate
  and and_3 (and_3_out, ~Opcode[0], Opcode[1], ~Opcode[2]);  // AND_Gate
  and and_4 (and_4_out, Opcode[0], Opcode[1], ~Opcode[2]);  // AND_Gate
  and and_5 (and_5_out, Opcode[0], ~Opcode[1], Opcode[2]);  // AND_Gate
  and and_6 (and_6_out, ~Opcode[0], ~Opcode[1], Opcode[2]);  // AND_Gate
  and and_7 (and_7_out, ~Opcode[0], Opcode[1], Opcode[2]);  // AND_Gate
  buf buffer_1 (Clock_2, Clock);
  and and_8 (and_8_out, Opcode[0], Opcode[1], Opcode[2]);
  and and_9 (and_9_out, and_5_out, flag);
  or or_1 (MB_IC, and_9_out, and_6_out);
  or or_2 (or_2_out, Zero, and_2_out, and_3_out);
  not not_1 (not_1_out, and_8_out);
  not not_2 (not_2_out, and_9_out);
  or or_3 (or_3_out, counter_1_t1, ldOP);
  or or_4 (or_4_out, or_2_out, and_7_out);
  or or_5 (Sub, and_7_out, and_2_out);
  xor xor_1 (xor_1_out, and_4_out, 1'b1);
  not not_3 (not_3_out, Opcode[2]);
  and and_10 (A_MB, counter_1_t4, and_4_out);
  and and_11 (and_11_out, counter_1_t3, and_4_out);
  or or_6 (R, or_3_out, xor_1_out);
  not not_4 (not_4_out, and_7_out);
  and and_12 (ldxmp, counter_1_t6, and_7_out);
  or or_7 (ldMB, counter_1_t1, counter_1_t4);
  and and_13 (and_13_out, counter_1_t3, or_4_out);
  and and_14 (ldB, counter_1_t5, or_4_out);
  and and_15 (and_15_out, counter_1_t6, or_4_out);
  and and_16 (ldIC, counter_1_t7, not_1_out);
  or or_8 (IC_1_IC, not_3_out, not_2_out);
  or or_9 (MB_MA, and_13_out, and_11_out);
  or or_10 (or_10_out, and_13_out, IC_MA);
  and and_17 (ldA, and_15_out, not_4_out);
  or or_11 (ldMA, or_10_out, and_11_out);
endmodule
